# Fritzing sketch schematic (saved by Fritzing 0.9.2b)
breadboards: 1

parts:
  Part1 = Arduino Uno (Rev3)
  TFT_Screen = 1.8" TFT Display with uSD  # not connected
  GND = Header 1 [package=1x01_offset]
  VCC = Header 1 [package=1x01_offset]
  SCL = Header 1 [package=1x01_offset]
  SDA = Header 1 [package=1x01_offset]
  DC = Header 1 [package=1x01_offset]
  RES = Header 1 [package=1x01_offset]
  CS = Header 1 [package=1x01_offset]
  SD_CS = Header 1 [package=1x01_offset]
  MISO = Header 1 [package=1x01_offset]
  X = Header 1 [package=1x01_offset]
  Y = Header 1 [package=1x01_offset]
  SPKR1 = Loudspeaker
  LED1 = LED - 5mm [color="Red (633nm)" package="5 mm [THT]"]
  R1 = Resistor [tolerance=±5% resistance=220 package=THT]
  R2 = Rotary Potentiometer (Small) [maximum_resistance=100kΩ package=THT]
  R3 = Resistor [tolerance=±5% resistance=220 package=THT]
  R4 = Resistor [tolerance=±5% resistance=220 package=THT]
  R5 = Resistor [tolerance=±5% resistance=220 package=THT]
  R6 = Resistor [tolerance=±5% resistance=220 package=THT]
  Part2 = Thumb Joystick  # not connected
  +5V = Header 1 [package=1x01_offset]
  GND_2 = Header 1 [package=1x01_offset]
  VRx = Header 1 [package=1x01_offset]
  VRy = Header 1 [package=1x01_offset]
  SW = Header 1 [package=1x01_offset]

nets:
  N1: Part1.A0, X.1
  N2: Part1.A1, SPKR1.pin2
  N3: Part1.A2, Y.1
  N4: Part1.A3, VRx.1
  N5: Part1.A4/SDA, VRy.1
  N6: Part1.A5/SCL, R2.wiper
  N7: Part1.D8, RES.1
  N8: Part1.D9_PWM, DC.1
  N9: Part1.D10_PWM/SS, CS.1
  N10: Part1.D11_PWM/MOSI, SDA.1
  N11: Part1.D12/MISO, MISO.1
  N12: Part1.D13/SCK, SCL.1
  N13: Part1.D2, Part1.D3_PWM, Part1.D6_PWM, Part1.D7, Part1.5V, VCC.1, R2.leg2, R3.Pin_1, R4.Pin_1, R5.Pin_1, R6.Pin_1, +5V.1
  N14: Part1.D4, SD_CS.1
  N15: Part1.D5_PWM, SW.1
  N16: Part1.GND, GND.1, R1.Pin_0, R2.leg1, R3.Pin_0, R4.Pin_0, R5.Pin_0, R6.Pin_0, GND_2.1
  N17: SPKR1.pin1, LED1.anode
  N18: LED1.cathode, R1.Pin_1

custom parts:
  1.8" TFT Display with uSD: 1.8" TFT Display with SPI control and MicroSD card
